# Fritzing sketch raspberry-sensors (saved by Fritzing 0.9.3b)

parts:
  Raspberry_Pi_1 = Raspberry Pi 3 [part_number=RPI-3-V1.2]
  Part2 = BME280 Breakout
  JP1 = Header 8 [package=bm08b-srss-tb]

nets:
  3V3: Raspberry_Pi_1.3v3, Raspberry_Pi_1.3V3, Part2.3.3V, JP1.VCC
  N1: Raspberry_Pi_1.GPIO2, Part2.SDI/SDA
  N2: Raspberry_Pi_1.GPIO3, Part2.SCK/SCL
  GND: Raspberry_Pi_1.GND, Part2.GND, JP1.GND, JP1.BUSY
  N3: Raspberry_Pi_1.GPIO22, JP1.CS
  N4: Raspberry_Pi_1.GPIO10, JP1.DIN
  N5: Raspberry_Pi_1.GPIO9, JP1.CLK
  N6: Raspberry_Pi_1.GPIO13, JP1.RST
  N7: Raspberry_Pi_1.GPIO12, JP1.DC

notes:
  5V DC via Instruments circuit
  USB GPS dongle
  Connected to WiFi AP
  Barometer, humidity, temperature
  USB RTL-SDR dongle
  Audio connection to JBL Go 2
  WaveShare 4.2 e-Paper module

custom parts:
  Header 8: Header 8 Standard 8-pin 0.1 header. Use with straight break away headers (SKU : PRT-00116), right angle break away headers (PRT-00553), swiss pins (PRT-00743), machine pins (PRT-00117), and female headers (PRT-00115).
